// Logisim project ALU.circ as structural Verilog: 1 circuit, main circuit main
module main (
  input  [15:0] AC,
  input  [15:0] DR,
  input  ADD,
  input  SUB,
  input  OR,
  input  AND,
  input  XOR,
  input  COM,
  input  SHL,
  input  SHR,
  input  in_11,
  output [15:0] OUTPUT,
  output LD_AC
);

  wire [15:0] adder_1_out, and_1_out, and_2_out, and_3_out, and_4_out, and_5_out, and_6_out, and_7_out,
       and_8_out, and_9_out, and_10_out, main_1_out, main_2_out, main_3_out, main_4_out, main_5_out,
       main_6_out, main_7_out, main_8_out, main_9_out, main_10_out_2, main_11_out_2, not_1_out, or_1_out,
       subtractor_1_out, xor_1_out;

  _1_TO_16_main main_1 (.IN(ADD), .OUT(main_1_out));
  _1_TO_16_main main_2 (.IN(SUB), .OUT(main_2_out));
  _1_TO_16_main main_3 (.IN(OR), .OUT(main_3_out));
  _1_TO_16_main main_4 (.IN(AND), .OUT(main_4_out));
  _1_TO_16_main main_5 (.IN(XOR), .OUT(main_5_out));
  _1_TO_16_main main_6 (.IN(COM), .OUT(main_6_out));
  _1_TO_16_main main_7 (.IN(SHL), .OUT(main_7_out));
  _1_TO_16_main main_8 (.IN(SHR), .OUT(main_8_out));
  Adder #(.width(16)) adder_1 (.a(AC), .b(DR), .out(adder_1_out));  // open: cin, cout
  _1_TO_16_main main_9 (.IN(in_11), .OUT(main_9_out));
  Subtractor #(.width(16)) subtractor_1 (.a(AC), .b(DR), .out(subtractor_1_out));  // open: bin, bout
  assign or_1_out = AC | DR;  // OR_Gate or_1, 16 bits wide
  assign and_1_out = AC & DR;  // AND_Gate and_1, 16 bits wide
  assign xor_1_out = AC ^ DR;  // XOR_Gate xor_1, 16 bits wide
  assign not_1_out = ~AC;  // NOT_Gate not_1, 16 bits wide
  SHL_main main_10 (.in_1(AC), .out_2(main_10_out_2));
  SHR_main main_11 (.in_1(AC), .out_2(main_11_out_2));
  assign and_2_out = adder_1_out & main_1_out;  // AND_Gate and_2, 16 bits wide
  assign and_3_out = subtractor_1_out & main_2_out;  // AND_Gate and_3, 16 bits wide
  assign and_4_out = or_1_out & main_3_out;  // AND_Gate and_4, 16 bits wide
  assign and_5_out = and_1_out & main_4_out;  // AND_Gate and_5, 16 bits wide
  assign and_6_out = xor_1_out & main_5_out;  // AND_Gate and_6, 16 bits wide
  assign and_7_out = not_1_out & main_6_out;  // AND_Gate and_7, 16 bits wide
  assign and_8_out = main_10_out_2 & main_7_out;  // AND_Gate and_8, 16 bits wide
  assign and_9_out = main_11_out_2 & main_8_out;  // AND_Gate and_9, 16 bits wide
  assign and_10_out = DR & main_9_out;  // AND_Gate and_10, 16 bits wide
  assign OUTPUT = and_2_out | and_3_out | and_4_out | and_5_out | and_10_out | and_6_out | and_7_out | and_8_out | and_9_out;  // OR_Gate or_2, 16 bits wide
  or or_3 (LD_AC, ADD, SUB, OR, AND, XOR, COM, SHL, SHR, in_11);
endmodule
