// Logisim project CAR.circ as structural Verilog: 1 circuit, main circuit main
module main (
  input  CLK,
  input  [6:0] INPUT,
  output [6:0] OUT_UT
);

  D_Flip_Flop d_ff_1 (.clk(CLK), .D(INPUT[0]), .Q(OUT_UT[0]));  // open: Qn, preset, en, reset
  D_Flip_Flop d_ff_2 (.clk(CLK), .D(INPUT[1]), .Q(OUT_UT[1]));  // open: Qn, preset, en, reset
  D_Flip_Flop d_ff_3 (.clk(CLK), .D(INPUT[2]), .Q(OUT_UT[2]));  // open: Qn, preset, en, reset
  D_Flip_Flop d_ff_4 (.clk(CLK), .D(INPUT[3]), .Q(OUT_UT[3]));  // open: Qn, preset, en, reset
  D_Flip_Flop d_ff_5 (.clk(CLK), .D(INPUT[4]), .Q(OUT_UT[4]));  // open: Qn, preset, en, reset
  D_Flip_Flop d_ff_6 (.clk(CLK), .D(INPUT[5]), .Q(OUT_UT[5]));  // open: Qn, preset, en, reset
  D_Flip_Flop d_ff_7 (.clk(CLK), .D(INPUT[6]), .Q(OUT_UT[6]));  // open: Qn, preset, en, reset
endmodule
