// Logisim project COMP2.circ as structural Verilog: 1 circuit, main circuit main
module main (
  output [15:0] out_1,
  output [15:0] out_2
);

  wire clock_1_out, decoder_1_out1, decoder_1_out2, decoder_1_out3, decoder_1_out4, decoder_1_out5,
       decoder_1_out6, decoder_1_out7, decoder_2_out1, decoder_2_out2, decoder_2_out3, decoder_2_out4,
       decoder_2_out5, decoder_2_out6, decoder_2_out7, decoder_3_out1, decoder_3_out2, decoder_3_out3,
       decoder_3_out4, decoder_3_out5, decoder_3_out6, main_5_i, main_6_ld_ac, main_7_ac, main_7_ac_15,
       not_1_out, or_1_out, or_2_out, or_5_out;
  wire [1:0] or_4_out;
  wire [2:0] main_1_f1, main_1_f2, main_1_f3;
  wire [10:0] main_2_output, main_3_output, main_8_out_2, multiplexer_1_out;
  wire [15:0] main_4_out_2, main_6_output, multiplexer_2_out, ram_1_data;

  Clock clock_1 (.out(clock_1_out));
  CONTROL_UNIT_main main_1 (
    .CLK(clock_1_out), .EXTERNAL_MAP({1'b0, out_1[14:11], 2'b00}), .I(main_5_i), .S(main_7_ac_15),
    .Z(not_1_out), .F3(main_1_f3), .F2(main_1_f2), .F1(main_1_f1));
  Decoder #(.select(3), .disabled(0), .enable("false")) decoder_1 (
    .out1(decoder_1_out1), .out2(decoder_1_out2), .out3(decoder_1_out3), .out4(decoder_1_out4),
    .out5(decoder_1_out5), .out6(decoder_1_out6), .out7(decoder_1_out7), .sel(main_1_f1));  // open: out0
  Decoder #(.select(3), .disabled(0), .enable("false")) decoder_2 (
    .out1(decoder_2_out1), .out2(decoder_2_out2), .out3(decoder_2_out3), .out4(decoder_2_out4),
    .out5(decoder_2_out5), .out6(decoder_2_out6), .out7(decoder_2_out7), .sel(main_1_f2));  // open: out0
  Decoder #(.select(3), .disabled(0), .enable("false")) decoder_3 (
    .out1(decoder_3_out1), .out2(decoder_3_out2), .out3(decoder_3_out3), .out4(decoder_3_out4),
    .out5(decoder_3_out5), .out6(decoder_3_out6), .sel(main_1_f3));  // open: out0, out7
  or or_1 (or_1_out, decoder_2_out4, decoder_2_out5, decoder_2_out7);
  or or_2 (or_2_out, decoder_1_out5, decoder_1_out6);
  or or_3 (or_4_out[1], decoder_2_out4, decoder_2_out5);
  or or_4 (or_4_out[0], decoder_2_out5, decoder_2_out6);
  Multiplexer #(.width(11), .enable("false")) multiplexer_1 (
    .in0(main_3_output), .in1(main_8_out_2), .out(multiplexer_1_out), .sel(decoder_1_out5));
  _12_BIT_main main_2 (
    .CLK(clock_1_out), .CLR(1'b0), .LOAD(or_2_out), .INCR(1'b0), .INPUT(multiplexer_1_out),
    .OUTPUT(main_2_output));
  _12_BIT_main main_3 (
    .CLK(clock_1_out), .CLR(1'b0), .LOAD(decoder_3_out6), .INCR(decoder_3_out5), .INPUT(main_2_output),
    .OUTPUT(main_3_output));
  _11to16_main main_4 (.in_1(main_3_output), .out_2(main_4_out_2));
  or or_5 (or_5_out, decoder_1_out7, decoder_2_out4);
  RAM #(.addrWidth(11), .dataWidth(16), .bus("separate")) ram_1 (
    .addr(main_2_output), .din(out_1), .data(ram_1_data), .str(decoder_1_out7), .sel(or_5_out),
    .clk(clock_1_out), .ld(decoder_2_out4));  // open: clr
  Multiplexer #(.select(2), .width(16), .enable("false")) multiplexer_2 (
    .in1(main_4_out_2), .in2(ram_1_data), .in3(out_2), .out(multiplexer_2_out), .sel(or_4_out));  // open: in0
  DR_main main_5 (
    .CLK(clock_1_out), .CLR(1'b0), .LOAD(or_1_out), .INCR(decoder_2_out6), .INPUT(multiplexer_2_out),
    .OUTPUT(out_1), .I(main_5_i));
  ALU_main main_6 (
    .AC(out_2), .DR(out_1), .ADD(decoder_1_out1), .SUB(decoder_2_out1), .OR(decoder_2_out2),
    .AND(decoder_2_out3), .XOR(decoder_3_out1), .COM(decoder_3_out2), .SHL(decoder_3_out3),
    .SHR(decoder_3_out4), .in_11(decoder_1_out4), .OUTPUT(main_6_output), .LD_AC(main_6_ld_ac));
  AC_main main_7 (
    .CLK(clock_1_out), .CLR(decoder_1_out2), .LOAD(main_6_ld_ac), .INCR(decoder_1_out3),
    .INPUT(main_6_output), .OUTPUT(out_2), .AC_15(main_7_ac_15), .AC(main_7_ac));
  not not_1 (not_1_out, main_7_ac);
  _16to11_main main_8 (.in_1(out_1), .out_2(main_8_out_2));

  // Notes on the sheet:
  //   CONTOL UNIT
  //   F1
  //   F2
  //   F3
  //   AR
  //   PC
  //   MEMORY
  //   DR
  //   ALU
  //   AC
endmodule
