// Logisim project CONTROL UNIT.circ as structural Verilog: 1 circuit, main circuit main
module main (
  input  CLK,
  input  [6:0] EXTERNAL_MAP,
  input  I,
  input  S,
  input  Z,
  output [2:0] F3,
  output [2:0] F2,
  output [2:0] F1
);

  wire d_ff_1_q, d_ff_2_q, d_ff_3_q, main_1_ld;
  wire [1:0] main_1_output;
  wire [6:0] main_2_out_ut, main_3_output, main_4_out_ut, multiplexer_1_out;
  wire [10:0] rom_1_data;

  D_Flip_Flop d_ff_1 (.clk(CLK), .D(I), .Q(d_ff_1_q));  // open: Qn, preset, en, reset
  D_Flip_Flop d_ff_2 (.clk(CLK), .D(S), .Q(d_ff_2_q));  // open: Qn, preset, en, reset
  D_Flip_Flop d_ff_3 (.clk(CLK), .D(Z), .Q(d_ff_3_q));  // open: Qn, preset, en, reset
  INPUTLOGIC_main main_1 (
    .I(d_ff_1_q), .S(d_ff_2_q), .Z(d_ff_3_q), .CD(rom_1_data[10:9]), .BR(rom_1_data[8:7]), .LD(main_1_ld),
    .OUTPUT(main_1_output));
  Multiplexer #(.select(2), .width(7), .enable("false")) multiplexer_1 (
    .in0(main_3_output), .in1(rom_1_data[6:0]), .in2(main_2_out_ut), .in3(EXTERNAL_MAP),
    .out(multiplexer_1_out), .sel(main_1_output));
  SBR_main main_2 (.INPUT(main_3_output), .LD(main_1_ld), .OUT_UT(main_2_out_ut));
  INCREMENTER_main main_3 (.INPTUT(main_4_out_ut), .OUTPUT(main_3_output));
  CAR_main main_4 (.INPUT(multiplexer_1_out), .CLK(CLK), .OUT_UT(main_4_out_ut));
  ROM #(.addrWidth(7), .dataWidth(20)) rom_1 (.addr(main_4_out_ut), .data({F1, F2, F3, rom_1_data}));  // open: sel
endmodule
