// Logisim project INCREMENTER.circ as structural Verilog: 1 circuit, main circuit main
module main (
  input  [6:0] INPTUT,
  output [6:0] OUTPUT
);

  wire main_1_p4, main_2_p3, main_3_p4, main_4_p3, main_5_p3, main_6_p3;

  // HA_main main_1: pin names not known; wires that end beside it: INPTUT[0], 1'b1, INPTUT[0], main_1_p4, OUTPUT[0]
  // HA_main main_2: pin names not known; wires that end beside it: main_1_p4, INPTUT[1], main_2_p3, OUTPUT[1]
  // HA_main main_3: pin names not known; wires that end beside it: INPTUT[0], main_2_p3, INPTUT[2], main_3_p4, OUTPUT[2]
  // HA_main main_4: pin names not known; wires that end beside it: main_3_p4, INPTUT[3], main_4_p3, OUTPUT[3]
  // HA_main main_5: pin names not known; wires that end beside it: main_4_p3, INPTUT[4], main_5_p3, OUTPUT[4]
  // HA_main main_6: pin names not known; wires that end beside it: main_5_p3, INPTUT[5], main_6_p3, OUTPUT[5]
  // HA_main main_7: pin names not known; wires that end beside it: main_6_p3, INPTUT[6], OUTPUT[6]

  // Notes on the sheet:
  //   INCREMENTER
endmodule
