// Logisim project INPUTLOGIC.circ as structural Verilog: 1 circuit, main circuit main
module main (
  input  I,
  input  S,
  input  Z,
  input  [1:0] CD,
  input  [1:0] BR,
  output LD,
  output [1:0] OUTPUT
);

  wire and_1_out, and_3_out, multiplexer_1_out, not_1_out;

  Multiplexer #(.select(2), .enable("false")) multiplexer_1 (
    .in0(1'b1), .in1(I), .in2(S), .in3(Z), .out(multiplexer_1_out), .sel(CD));
  and and_1 (and_1_out, BR[0], BR[1]);
  and and_2 (LD, multiplexer_1_out, BR[0], not_1_out);
  and and_3 (and_3_out, multiplexer_1_out, not_1_out);
  not not_1 (not_1_out, BR[1]);
  or or_1 (OUTPUT[0], and_3_out, and_1_out);

  assign OUTPUT[1] = BR[1];

  // Notes on the sheet:
  //   INPUT LOGIC
endmodule
