// Logisim project SBR.circ as structural Verilog: 1 circuit, main circuit main
module main (
  input  LD,
  input  [6:0] INPUT,
  output [6:0] OUT_UT
);

  D_Flip_Flop d_ff_1 (.D(INPUT[0]), .Q(OUT_UT[0]), .en(LD));  // open: clk, Qn, preset, reset
  D_Flip_Flop d_ff_2 (.D(INPUT[1]), .Q(OUT_UT[1]), .en(LD));  // open: clk, Qn, preset, reset
  D_Flip_Flop d_ff_3 (.D(INPUT[2]), .Q(OUT_UT[2]), .en(LD));  // open: clk, Qn, preset, reset
  D_Flip_Flop d_ff_4 (.D(INPUT[3]), .Q(OUT_UT[3]), .en(LD));  // open: clk, Qn, preset, reset
  D_Flip_Flop d_ff_5 (.D(INPUT[4]), .Q(OUT_UT[4]), .en(LD));  // open: clk, Qn, preset, reset
  D_Flip_Flop d_ff_6 (.D(INPUT[5]), .Q(OUT_UT[5]), .en(LD));  // open: clk, Qn, preset, reset
  D_Flip_Flop d_ff_7 (.D(INPUT[6]), .Q(OUT_UT[6]), .en(LD));  // open: clk, Qn, preset, reset

  // Notes on the sheet:
  //   SBR REGISTER
endmodule
